# Fritzing sketch project_1 (saved by Fritzing 0.9.4)
breadboards: 1

parts:
  元件1 = Arduino Uno (Rev3)
  LED1 = LED - 5mm [color="Red (633nm)" package="5 mm [THT]"]
  R1 = Resistor [tolerance=±5% resistance=220 package=THT]
  R2 = Resistor [tolerance=±5% resistance=220 package=THT]
  LED2 = LED - 5mm [color="Red (633nm)" package="5 mm [THT]"]
  LED3 = LED - 5mm [color="Red (633nm)" package="5 mm [THT]"]
  LED4 = LED - 5mm [color="Red (633nm)" package="5 mm [THT]"]
  R3 = Resistor [tolerance=±5% resistance=220 package=THT]
  R4 = Resistor [tolerance=±5% resistance=220 package=THT]
  S1 = Pushbutton [package="[THT]"]

nets:
  N1: 元件1.GND, LED1.cathode, LED2.cathode, LED3.cathode, LED4.cathode, S1.Pin_3, S1.Pin_4
  N2: 元件1.D2, R4.Pin_1
  N3: 元件1.D3_PWM, R3.Pin_1
  N4: 元件1.D4, R2.Pin_1
  N5: 元件1.D5_PWM, R1.Pin_1
  N6: 元件1.D7, S1.Pin_1, S1.Pin_2
  N7: LED1.anode, R1.Pin_0
  N8: R2.Pin_0, LED2.anode
  N9: LED3.anode, R3.Pin_0
  N10: LED4.anode, R4.Pin_0
