# Fritzing sketch project_2 (saved by Fritzing 0.9.4)
breadboards: 1

parts:
  LED1 = LED - 5mm [color="Red (633nm)" package="5 mm [THT]"]
  元件1 = Arduino Uno (Rev3)
  R1 = Photocell (LDR) [package=THT]
  R2 = Resistor [tolerance=±5% resistance=220 package=THT]

nets:
  N1: LED1.cathode, 元件1.GND, R2.Pin_1
  N2: LED1.anode, 元件1.D9_PWM
  N3: 元件1.A0, R1.pin_1, R2.Pin_0
  N4: 元件1.5V, R1.pin_0
