# Fritzing sketch project_3 (saved by Fritzing 0.9.4)
breadboards: 1

parts:
  元件1 = Arduino Uno (Rev3)
  J1 = Piezo Speaker
  S1 = Pushbutton [package="[THT]"]
  S2 = Pushbutton [package="[THT]"]
  S3 = Pushbutton [package="[THT]"]
  R2 = Resistor [tolerance=±5% resistance=220 package=THT]
  R3 = Resistor [tolerance=±5% resistance=220 package=THT]
  OLED_I2C1 = OLED 128x64 I2C Monochrome Display
  hc-sr1 = hc-sr04
  R4 = Resistor [tolerance=±5% resistance=220 package=THT]

nets:
  N1: 元件1.A4/SDA, OLED_I2C1.SDA
  N2: 元件1.A5/SCL, OLED_I2C1.SCK
  GND: 元件1.GND, J1.pin1, R2.Pin_0, R3.Pin_0, OLED_I2C1.GND, hc-sr1.GND, R4.Pin_0
  N3: 元件1.D2, hc-sr1.Trig
  N4: 元件1.D4, S3.Pin_1, S3.Pin_2
  N5: 元件1.D5_PWM, S2.Pin_1, S2.Pin_2
  N6: 元件1.D6_PWM, S1.Pin_1, S1.Pin_2
  N7: 元件1.D7, hc-sr1.Echo
  5V: 元件1.5V, J1.pin2, OLED_I2C1.VDD, hc-sr1.VCC
  N8: S1.Pin_3, S1.Pin_4, R4.Pin_1
  N9: S2.Pin_3, S2.Pin_4, R2.Pin_1
  N10: S3.Pin_3, S3.Pin_4, R3.Pin_1
