# Fritzing sketch project_4 (saved by Fritzing 0.9.4)
breadboards: 1

parts:
  元件1 = Arduino Uno (Rev3)
  元件2 = SPI OLED Monochrome 128x64 0.96 inch
  元件3 = Real Time Clock Module - DS1307 RTC Breakout Board
  J1 = Piezo Speaker

nets:
  N1: 元件1.A4/SDA, 元件3.SDA
  N2: 元件1.A5/SCL, 元件3.SCL
  N3: 元件1.D8, 元件2.RES
  N4: 元件1.D10_PWM/SS, 元件2.CS
  N5: 元件1.D11_PWM/MOSI, 元件2.SDA
  N6: 元件1.D12/MISO, 元件2.DC
  N7: 元件1.D13/SCK, 元件2.SCK
  GND: 元件1.GND, 元件2.GND, 元件3.GND, J1.pin1
  5V: 元件1.5V, 元件2.VDD, 元件3.5V, J1.pin2

custom parts:
  SPI OLED Monochrome 128x64 0.96 inch: Unknown 128x64 0.96 inch 128x64 SPI Monochrome OLED display
