# Fritzing sketch project_4 (saved by Fritzing 0.9.4)
breadboards: 1

parts:
  元件1 = Arduino Uno (Rev3)
  元件2 = SPI OLED Monochrome 128x64 0.96 inch
  元件3 = Real Time Clock Module - DS1307 RTC Breakout Board
  J1 = Piezo Speaker
  S1 = Pushbutton [package="[THT]"]
  S2 = Pushbutton [package="[THT]"]
  S3 = Pushbutton [package="[THT]"]
  R1 = Resistor [tolerance=±5% resistance=220 package=THT]
  R2 = Resistor [tolerance=±5% resistance=220 package=THT]
  R3 = Resistor [tolerance=±5% resistance=220 package=THT]

nets:
  N1: 元件1.A4/SDA, 元件3.SDA
  N2: 元件1.A5/SCL, 元件3.SCL
  N3: 元件1.D8, 元件2.RES
  N4: 元件1.D11_PWM/MOSI, 元件2.SDA
  N5: 元件1.D13/SCK, 元件2.SCK
  N6: 元件1.D2, S3.Pin_3, S3.Pin_4, R3.Pin_0
  N7: 元件1.D3_PWM, S2.Pin_3, S2.Pin_4, R2.Pin_0
  N8: 元件1.D4, S1.Pin_3, S1.Pin_4, R1.Pin_0
  5V: 元件1.5V, 元件2.VDD, 元件3.5V, J1.pin2
  GND: 元件1.GND, 元件2.GND, 元件3.GND, J1.pin1, R1.Pin_1, R2.Pin_1, R3.Pin_1
  N9: S1.Pin_1, S1.Pin_2
  N10: S2.Pin_1, S2.Pin_2
  N11: S3.Pin_1, S3.Pin_2

custom parts:
  SPI OLED Monochrome 128x64 0.96 inch: Unknown 128x64 0.96 inch 128x64 SPI Monochrome OLED display
