# Fritzing sketch project_5 (saved by Fritzing 0.9.4)
breadboards: 1

parts:
  OLED_I2C1 = OLED 128x64 I2C Monochrome Display
  元件1 = Arduino Uno (Rev3)
  J1 = Piezo Speaker
  DHT11_1 = DHT11 module
  M1 = fc-51 [package=THT]
  M2 = fc-51 [package=THT]

nets:
  N1: OLED_I2C1.SDA, 元件1.A4/SDA
  N2: OLED_I2C1.SCK, 元件1.A5/SCL
  VDD: OLED_I2C1.VDD, 元件1.D3_PWM, 元件1.5V, J1.pin2, DHT11_1.VCC, M1.pin1, M1.pin3, M2.pin3
  GND: OLED_I2C1.GND, 元件1.GND, J1.pin1, DHT11_1.GND, M1.pin2, M2.pin2
  N3: 元件1.D2, DHT11_1.DATA
  N4: 元件1.D4, M2.pin1

custom parts:
  DHT11 module: https://cdn-learn.adafruit.com/downloads/pdf/dht.pdf DHT11 black pcb module reference by:https://github.com/adafruit/Fritzing-Library/blob/master/parts/DHT11%20Humitidy%20and%20Temperature%20Sensor.fzpz
